# Fritzing sketch room-control-unit-scheme (saved by Fritzing 0.9.3b)
breadboards: 3

parts:
  Part2 = RFID-RC522-v3
  Part3 = RFID-RC522-v3
  Part4 = RFID-RC522-v3
  Part5 = Arduino Mega 2560 (Rev3)
  DHT1 = DHT11 Humitidy and Temperature Sensor
  R1 = Resistor [tolerance=±5% resistance=10k package="1206 [SMD]"]
  DHT2 = DHT11 Humitidy and Temperature Sensor
  R2 = Resistor [tolerance=±5% resistance=10k package="1206 [SMD]"]
  S1 = Pushbutton [package="[SMD]"]
  R3 = Resistor [tolerance=±5% resistance=10k package="1206 [SMD]"]
  R4 = PHOTOCELL [package=photocell]
  R5 = Resistor [tolerance=±5% resistance=10k package="1206 [SMD]"]
  R6 = Resistor [tolerance=±5% resistance=10k package="1206 [SMD]"]
  R7 = PHOTOCELL [package=photocell]
  PIR1 = PIR sensor
  PIR2 = PIR sensor
  LED1 = LED - 3mm [color="White (4500K)" package="3 mm [THT]"]
  LED2 = LED - 3mm [color="White (4500K)" package="3 mm [THT]"]
  LED3 = LED - 3mm [color="White (4500K)" package="3 mm [THT]"]
  R9 = Resistor [tolerance=±5% resistance=220 package="1206 [SMD]"]
  R10 = Resistor [tolerance=±5% resistance=220 package="1206 [SMD]"]
  F1 = Fan - Ventilador [package=THT]
  F2 = Fan - Ventilador [package=THT]
  LED4 = LED - 3mm [color="Red (633nm)" package="3 mm [THT]"]
  LED5 = LED - 3mm [color="Blue (470nm)" package="3 mm [THT]"]
  LED6 = LED - 3mm [color="Red (633nm)" package="3 mm [THT]"]
  LED7 = LED - 3mm [color="Blue (470nm)" package="3 mm [THT]"]
  R8 = Resistor [tolerance=±5% resistance=220 package="1206 [SMD]"]
  R11 = Resistor [tolerance=±5% resistance=220 package="1206 [SMD]"]
  R12 = Resistor [tolerance=±5% resistance=220 package="1206 [SMD]"]
  R13 = Resistor [tolerance=±5% resistance=220 package="1206 [SMD]"]
  R14 = Resistor [tolerance=±5% resistance=220 package="1206 [SMD]"]
  IC1 = L293D [package=THT]
  Power_plug1 = Power plug

nets:
  N1: Part2.SDA, Part5.D35
  N2: Part2.SCK, Part3.SCK, Part4.SCK, Part5.D52
  N3: Part2.MOSI, Part3.MOSI, Part4.MOSI, Part5.D51
  N4: Part2.MISO, Part3.MISO, Part4.MISO, Part5.D50
  GND: Part2.GND, Part3.GND, Part4.GND, Part5.GND, DHT1.GND, DHT2.GND, R3.Pin_1, R6.Pin_1, PIR1.GND, PIR2.GND, LED1.cathode, LED2.cathode, LED3.cathode, LED4.cathode, LED5.cathode, LED6.cathode, LED7.cathode, IC1.0V, IC1.In_2, IC1.In_3, Power_plug1.GND
  N5: Part2.RST, Part3.RST, Part4.RST, Part5.D49
  3.3V: Part2.3.3V, Part3.3.3V, Part4.3.3V, Part5.3V3
  N6: Part3.SDA, Part5.D33
  N7: Part4.SDA, Part5.D31
  N8: Part5.A0, R4.P$2, R5.Pin_0
  N9: Part5.A1, R6.Pin_0, R7.P$2
  N10: Part5.D13_PWM, DHT1.DATA, R1.Pin_0
  N11: Part5.D12_PWM, DHT2.DATA, R2.Pin_0
  N12: Part5.D11_PWM, S1.Pin_1, S1.Pin_2, R3.Pin_0
  N13: Part5.D10_PWM, PIR1.SIG
  N14: Part5.D9_PWM, PIR2.SIG
  N15: Part5.D8_PWM, LED1.anode, R8.Pin_0, R8.Pin_1
  VDD: Part5.5V, DHT1.VDD, R1.Pin_1, DHT2.VDD, R2.Pin_1, S1.Pin_3, S1.Pin_4, R4.P$1, R7.P$1, PIR1.VDD, PIR2.VDD, IC1.In_1, IC1.In_4, IC1.+V
  N16: Part5.D0_RX0, LED7.anode, R14.Pin_0, R14.Pin_1
  N17: Part5.D1_TX0, LED6.anode, R13.Pin_0, R13.Pin_1
  N18: Part5.D2_PWM, LED5.anode, R12.Pin_0, R12.Pin_1
  N19: Part5.D3_PWM, LED4.anode, R11.Pin_0, R11.Pin_1
  N20: Part5.D4_PWM, IC1.Enable_2
  N21: Part5.D5_PWM, IC1.Enable_1
  N22: Part5.D6_PWM, LED2.anode, R10.Pin_0, R10.Pin_1
  N23: Part5.D7_PWM, LED3.anode, R9.Pin_0, R9.Pin_1
  N24: F1.5V, IC1.Out_4_(_Controlled_by_Enable_2_)
  N25: F1.GND, IC1.Out_3_(_Controlled_by_Enable_2_)
  N26: F2.5V, IC1.Out_1_(_Controlled_by_Enable_1_)
  N27: F2.GND, IC1.Out_2_(_Controlled_by_Enable_1_)
  N28: IC1.+Vmotor, Power_plug1.VCC

notes:
  Implantable Device Bin
  Operating Room entrance/exit
  Pre-operating Room entrance/exit
  Operating Room humidity/temperature sensor
  Pre-operating Room humidity/temperature sensor
  Micro switch for operating table
  LS Pre
  LS OR
  Presence sensor
  Operating room
  Presence sensor
  Pre-operating room
  Surgical light
  Ambient-Light Operating Room
  Ambient-Light Pre-operating Room
  H OR
  C OR
  H Pre
  C Pre
  Pre-operating Room Ventilation
  Operating Room Ventilation
  12V

custom parts:
  RFID-RC522-v3: A simple China made RFID-RC522 Reader (6x4 cm); do check the pin labels, as this is a MFRC522 based clone.
  DHT11 Humitidy and Temperature Sensor: DHT11 Humidity and Temperature Sensor
  Fan - Ventilador: Ventilador de 2 pines, se encuentra comunmente en computadoras de escritorio
